// Logisim project Chips.circ as structural Verilog: 4 circuits, main circuit TTTC
module TTTC (
  input  btn,
  input  [1:0] vin,
  input  [1:0] hin,
  output vout,
  output hout,
  output [3:0] L0,
  output [3:0] L1,
  output [3:0] L2,
  output [3:0] L3
);

  wire and_1_out, not_1_out;
  wire [1:0] register_1_q;
  wire [15:0] bitselector_1_out;

  and and_1 (and_1_out, hin[1], vin[1]);
  Register #(.width(2), .trigger("low")) register_1 (
    .D({vin[0], hin[0]}), .en(and_1_out), .Q(register_1_q), .clk(1'b0));  // open: clr
  not not_1 (not_1_out, register_1_q[1]);
  BitSelector #(.width(32), .group(16)) bitselector_1 (
    .in(32'h9429f99f), .out(bitselector_1_out), .sel(register_1_q[0]));
  BitSelector #(.width(32), .group(16)) bitselector_2 (
    .in({{16{1'b0}}, bitselector_1_out}), .out({L3, L2, L1, L0}), .sel(not_1_out));
  // Probe on {L3, L2, L1, L0}

  assign hout = btn;
  assign vout = btn;
endmodule

module BPC (
  input  H0,
  input  H1,
  input  H2,
  input  V0,
  input  V1,
  input  V2,
  input  enable,
  output ready,
  output [3:0] XY
);
endmodule

module SDR (
  input  [1:0] symID,
  input  [3:0] XY,
  input  Enable,
  output [1:0] H0,
  output [1:0] H1,
  output [1:0] H2,
  output [1:0] V0,
  output [1:0] V1,
  output [1:0] V2
);

  wire [3:0] bitselector_1_out;

  BitSelector #(.group(4)) bitselector_1 (.in({XY, 4'b1111}), .out(bitselector_1_out), .sel(Enable));
  BitSelector #(.width(9), .group(3)) bitselector_2 (
    .in(9'h111), .out({V2[1], V1[1], V0[1]}), .sel(bitselector_1_out[1:0]));
  BitSelector #(.width(9), .group(3)) bitselector_3 (
    .in(9'h111), .out({H2[1], H1[1], H0[1]}), .sel(bitselector_1_out[3:2]));

  assign H0[0] = symID[0];
  assign H1[0] = symID[0];
  assign H2[0] = symID[0];
  assign V0[0] = symID[1];
  assign V1[0] = symID[1];
  assign V2[0] = symID[1];
endmodule

module GSDD (
  input  [1:0] score,
  input  clock,
  output win,
  output lose,
  output draw
);
endmodule
