// Logisim project Main.circ as structural Verilog: 1 circuit, main circuit Main
module Main (
);

  wire _O_O_out, _X_X_out, button_1_out, button_2_out, button_3_out, button_4_out, button_5_out,
       button_6_out, button_7_out, button_8_out, button_9_out, button_10_out, cdm_8_1_p2, cdm_8_1_p4,
       cdm_8_1_p5, cdm_8_1_p6, cdm_8_1_p7, cdm_8_1_p8, cdm_8_1_p9, cdm_8_1_p10, Cl, Code, data,
       decoder_1_out1, decoder_3_out0, decoder_3_out1, decoder_4_out0, decoder_4_out1, decoder_5_out0,
       decoder_5_out1, decoder_6_out0, decoder_6_out1, decoder_7_out0, decoder_7_out1, gsdd_1_draw,
       gsdd_1_lose, gsdd_1_win, I_Osel, In_out_prime, IO_3_out, IO_4_out, IO_5_out, IO_6_out, IO_7_out,
       IO_8_out, mem, nand_1_out, not_1_out, not_2_out, O___O_out, O_O__out, RAM, sdr_1_p4, X___X_out,
       X_X__out;
  wire [0:0] or_1_out, or_2_out, X_O_X_out;
  wire [1:0] sdr_1_p3, sdr_1_p5, sdr_1_p6, sdr_1_p7, sdr_1_p8, sdr_1_p9;
  wire [2:2] tttc_1_hout, tttc_1_vout, tttc_2_hout, tttc_3_hout, tttc_4_vout, tttc_7_vout;
  wire [3:0] I_Oadr, random_1_out, tttc_1_l0, tttc_1_l1, tttc_1_l2, tttc_1_l3, tttc_2_l0, tttc_2_l1,
       tttc_2_l2, tttc_2_l3, tttc_3_l0, tttc_3_l1, tttc_3_l2, tttc_3_l3, tttc_4_l0, tttc_4_l1, tttc_4_l2,
       tttc_4_l3, tttc_5_l0, tttc_5_l1, tttc_5_l2, tttc_5_l3, tttc_6_l0, tttc_6_l1, tttc_6_l2, tttc_6_l3,
       tttc_7_l0, tttc_7_l1, tttc_7_l2, tttc_7_l3, tttc_8_l0, tttc_8_l1, tttc_8_l2, tttc_8_l3, tttc_9_l0,
       tttc_9_l1, tttc_9_l2, tttc_9_l3;
  wire [7:0] bpc_1_ready, cdm_8_1_p14, cdm_8_1_p15, I_Odat, register_1_q, register_2_q, register_3_q,
       register_4_q;
  wire [7:4] cdm_8_1_p13;
  wire [7:6] X_X_X_out;

  // Probe on cdm_8_1_p4
  // Probe on cdm_8_1_p2
  Button button_1 (.out(button_1_out));
  Clock clock_1 (.out(Cl));
  and and_1 (I_Osel, not_1_out, Cl, data);
  GSDD gsdd_1 (.score(I_Odat[7:6]), .clock(sdr_1_p4), .win(gsdd_1_win), .lose(gsdd_1_lose), .draw(gsdd_1_draw));
  LED led_1 (.in(gsdd_1_win));
  // Probe on cdm_8_1_p5
  // Probe on cdm_8_1_p6
  // Probe on cdm_8_1_p7
  not not_1 (not_1_out, nand_1_out);
  and and_2 (RAM, nand_1_out, data);
  LED led_2 (.in(gsdd_1_lose));
  LED led_3 (.in(gsdd_1_draw));
  // SDR sdr_1: pin names not known; wires that end beside it: I_Odat[5:2], I_Odat[1:0], sdr_1_p3, sdr_1_p4, sdr_1_p5, sdr_1_p6, sdr_1_p7, sdr_1_p8, sdr_1_p9
  // Probe on cdm_8_1_p8
  // Probe on cdm_8_1_p9
  nand nand_1 (nand_1_out, cdm_8_1_p13[4], cdm_8_1_p13[5], cdm_8_1_p13[6], cdm_8_1_p13[7]);
  and IO_3 (IO_3_out, I_Osel, I_Oadr[0], I_Oadr[1], ~I_Oadr[2], ~I_Oadr[3]);  // AND_Gate
  // CdM_8 cdm_8_1: pin names not known; wires that end beside it: Cl, cdm_8_1_p2, button_1_out, cdm_8_1_p4, cdm_8_1_p5, cdm_8_1_p6, cdm_8_1_p7, cdm_8_1_p8, cdm_8_1_p9, cdm_8_1_p10, mem, In_out_prime, {cdm_8_1_p13, I_Oadr}, cdm_8_1_p14, cdm_8_1_p15
  Decoder #(.disabled(0)) decoder_1 (.out0(sdr_1_p4), .out1(decoder_1_out1), .sel(In_out_prime), .en(IO_3_out));
  TTTC tttc_1 (
    .vin(sdr_1_p3), .hin(sdr_1_p7), .btn(button_2_out), .vout(tttc_1_vout[2]), .hout(tttc_1_hout[2]),
    .L0(tttc_1_l0), .L1(tttc_1_l1), .L2(tttc_1_l2), .L3(tttc_1_l3));
  DotMatrix #(.inputtype("row"), .matrixcols(4), .matrixrows(4)) dotmatrix_1 (
    .row0(tttc_1_l0), .row1(tttc_1_l1), .row2(tttc_1_l2), .row3(tttc_1_l3));
  Button button_2 (.out(button_2_out));
  TTTC tttc_2 (
    .vin(sdr_1_p3), .hin(sdr_1_p8), .btn(button_3_out), .vout(tttc_1_vout[2]), .hout(tttc_2_hout[2]),
    .L0(tttc_2_l0), .L1(tttc_2_l1), .L2(tttc_2_l2), .L3(tttc_2_l3));
  DotMatrix #(.inputtype("row"), .matrixcols(4), .matrixrows(4)) dotmatrix_2 (
    .row0(tttc_2_l0), .row1(tttc_2_l1), .row2(tttc_2_l2), .row3(tttc_2_l3));
  Button button_3 (.out(button_3_out));
  TTTC tttc_3 (
    .vin(sdr_1_p3), .hin(sdr_1_p9), .btn(button_4_out), .vout(tttc_1_vout[2]), .hout(tttc_3_hout[2]),
    .L0(tttc_3_l0), .L1(tttc_3_l1), .L2(tttc_3_l2), .L3(tttc_3_l3));
  DotMatrix #(.inputtype("row"), .matrixcols(4), .matrixrows(4)) dotmatrix_3 (
    .row0(tttc_3_l0), .row1(tttc_3_l1), .row2(tttc_3_l2), .row3(tttc_3_l3));
  Button button_4 (.out(button_4_out));
  Decoder #(.disabled(0)) decoder_2 (.out0(Code), .out1(data), .sel(cdm_8_1_p10), .en(mem));
  assign I_Odat = not_2_out ? cdm_8_1_p14 : 8'bz;  // Controlled_Buffer controlled_buffer_1
  not not_2 (not_2_out, In_out_prime);
  assign cdm_8_1_p15 = In_out_prime ? I_Odat : 8'bz;  // Controlled_Buffer controlled_buffer_2
  TTTC tttc_4 (
    .vin(sdr_1_p5), .hin(sdr_1_p7), .btn(button_5_out), .vout(tttc_4_vout[2]), .hout(tttc_1_hout[2]),
    .L0(tttc_4_l0), .L1(tttc_4_l1), .L2(tttc_4_l2), .L3(tttc_4_l3));
  DotMatrix #(.inputtype("row"), .matrixcols(4), .matrixrows(4)) dotmatrix_4 (
    .row0(tttc_4_l0), .row1(tttc_4_l1), .row2(tttc_4_l2), .row3(tttc_4_l3));
  Button button_5 (.out(button_5_out));
  TTTC tttc_5 (
    .vin(sdr_1_p5), .hin(sdr_1_p8), .btn(button_6_out), .vout(tttc_4_vout[2]), .hout(tttc_2_hout[2]),
    .L0(tttc_5_l0), .L1(tttc_5_l1), .L2(tttc_5_l2), .L3(tttc_5_l3));
  DotMatrix #(.inputtype("row"), .matrixcols(4), .matrixrows(4)) dotmatrix_5 (
    .row0(tttc_5_l0), .row1(tttc_5_l1), .row2(tttc_5_l2), .row3(tttc_5_l3));
  Button button_6 (.out(button_6_out));
  TTTC tttc_6 (
    .vin(sdr_1_p5), .hin(sdr_1_p9), .btn(button_7_out), .vout(tttc_4_vout[2]), .hout(tttc_3_hout[2]),
    .L0(tttc_6_l0), .L1(tttc_6_l1), .L2(tttc_6_l2), .L3(tttc_6_l3));
  DotMatrix #(.inputtype("row"), .matrixcols(4), .matrixrows(4)) dotmatrix_6 (
    .row0(tttc_6_l0), .row1(tttc_6_l1), .row2(tttc_6_l2), .row3(tttc_6_l3));
  Button button_7 (.out(button_7_out));
  Pull_Resistor pull_resistor_1 (.node(I_Oadr[0]));
  Pull_Resistor pull_resistor_2 (.node(I_Oadr[1]));
  Pull_Resistor pull_resistor_3 (.node(I_Oadr[2]));
  Pull_Resistor pull_resistor_4 (.node(I_Oadr[3]));
  Pull_Resistor pull_resistor_5 (.node(cdm_8_1_p13[4]));
  Pull_Resistor pull_resistor_6 (.node(cdm_8_1_p13[5]));
  Pull_Resistor pull_resistor_7 (.node(cdm_8_1_p13[6]));
  Pull_Resistor pull_resistor_8 (.node(cdm_8_1_p13[7]));
  ROM rom_1 (.addr({cdm_8_1_p13, I_Oadr}), .data(I_Odat), .sel(Code));
  RAM ram_1 (.addr({cdm_8_1_p13, I_Oadr}), .data(I_Odat), .sel(RAM), .clk(Cl), .ld(In_out_prime));  // open: clr
  TTTC tttc_7 (
    .vin(sdr_1_p6), .hin(sdr_1_p7), .btn(button_8_out), .vout(tttc_7_vout[2]), .hout(tttc_1_hout[2]),
    .L0(tttc_7_l0), .L1(tttc_7_l1), .L2(tttc_7_l2), .L3(tttc_7_l3));
  DotMatrix #(.inputtype("row"), .matrixcols(4), .matrixrows(4)) dotmatrix_7 (
    .row0(tttc_7_l0), .row1(tttc_7_l1), .row2(tttc_7_l2), .row3(tttc_7_l3));
  Button button_8 (.out(button_8_out));
  TTTC tttc_8 (
    .vin(sdr_1_p6), .hin(sdr_1_p8), .btn(button_9_out), .vout(tttc_7_vout[2]), .hout(tttc_2_hout[2]),
    .L0(tttc_8_l0), .L1(tttc_8_l1), .L2(tttc_8_l2), .L3(tttc_8_l3));
  DotMatrix #(.inputtype("row"), .matrixcols(4), .matrixrows(4)) dotmatrix_8 (
    .row0(tttc_8_l0), .row1(tttc_8_l1), .row2(tttc_8_l2), .row3(tttc_8_l3));
  Button button_9 (.out(button_9_out));
  TTTC tttc_9 (
    .vin(sdr_1_p6), .hin(sdr_1_p9), .btn(button_10_out), .vout(tttc_7_vout[2]), .hout(tttc_3_hout[2]),
    .L0(tttc_9_l0), .L1(tttc_9_l1), .L2(tttc_9_l2), .L3(tttc_9_l3));
  DotMatrix #(.inputtype("row"), .matrixcols(4), .matrixrows(4)) dotmatrix_9 (
    .row0(tttc_9_l0), .row1(tttc_9_l1), .row2(tttc_9_l2), .row3(tttc_9_l3));
  Button button_10 (.out(button_10_out));
  Decoder #(.disabled(0)) decoder_3 (.out0(decoder_3_out0), .out1(decoder_3_out1), .sel(In_out_prime), .en(IO_4_out));
  and IO_4 (IO_4_out, I_Osel, ~I_Oadr[0], ~I_Oadr[1], I_Oadr[2], ~I_Oadr[3]);  // AND_Gate
  assign I_Odat = decoder_1_out1 ? {bpc_1_ready[7], 3'b000, bpc_1_ready[3:0]} : 8'bz;  // Controlled_Buffer controlled_buffer_3
  BPC bpc_1 (
    .H0(tttc_1_hout[2]), .H1(tttc_2_hout[2]), .H2(tttc_3_hout[2]), .V0(tttc_1_vout[2]), .V1(tttc_4_vout[2]),
    .V2(tttc_7_vout[2]), .reset(decoder_1_out1), .ready(bpc_1_ready[7]), .XY(bpc_1_ready[3:0]));
  Random #(.width(4)) random_1 (.clk(decoder_3_out0), .next(decoder_3_out0), .out(random_1_out));  // open: clr
  assign I_Odat = decoder_3_out1 ? {4'b0000, random_1_out} : 8'bz;  // Controlled_Buffer controlled_buffer_4
  Decoder #(.disabled(0)) decoder_4 (.out0(decoder_4_out0), .out1(decoder_4_out1), .sel(In_out_prime), .en(IO_5_out));
  and IO_5 (IO_5_out, I_Osel, I_Oadr[0], ~I_Oadr[1], I_Oadr[2], ~I_Oadr[3]);  // AND_Gate
  Register #(.trigger("high")) register_1 (
    .D(I_Odat), .en(decoder_4_out0), .Q(register_1_q), .clk(decoder_4_out0));  // open: clr
  and IO_8 (IO_8_out, I_Osel, ~I_Oadr[0], ~I_Oadr[1], ~I_Oadr[2], I_Oadr[3]);  // AND_Gate
  Decoder #(.disabled(0)) decoder_5 (.out0(decoder_5_out0), .out1(decoder_5_out1), .sel(In_out_prime), .en(IO_8_out));
  Register #(.trigger("high")) register_2 (
    .D(I_Odat), .en(decoder_5_out0), .Q(register_2_q), .clk(decoder_5_out0));  // open: clr
  assign I_Odat = decoder_4_out1 ? {{7{1'b0}}, or_1_out[0]} : 8'bz;  // Controlled_Buffer controlled_buffer_5
  and O_O_ (O_O__out, ~register_1_q[0], ~register_1_q[1], register_1_q[2], ~register_1_q[3], register_1_q[4], ~register_1_q[5]);  // AND_Gate
  and O___O (O___O_out, register_1_q[0], ~register_1_q[1], ~register_1_q[2], ~register_1_q[3], register_1_q[4], ~register_1_q[5]);  // AND_Gate
  and _O_O (_O_O_out, register_1_q[0], ~register_1_q[1], register_1_q[2], ~register_1_q[3], ~register_1_q[4], ~register_1_q[5]);  // AND_Gate
  or or_1 (or_1_out[0], _O_O_out, O___O_out, O_O__out);
  assign I_Odat = decoder_5_out1 ? {X_X_X_out, {6{1'b0}}} : 8'bz;  // Controlled_Buffer controlled_buffer_6
  and O_O_O (X_X_X_out[7], register_2_q[0], ~register_2_q[1], register_2_q[2], ~register_2_q[3], register_2_q[4], ~register_2_q[5]);  // AND_Gate
  and X_X_X (X_X_X_out[6], ~register_2_q[0], register_2_q[1], ~register_2_q[2], register_2_q[3], ~register_2_q[4], register_2_q[5]);  // AND_Gate
  Decoder #(.disabled(0)) decoder_6 (.out0(decoder_6_out0), .out1(decoder_6_out1), .sel(In_out_prime), .en(IO_6_out));
  and IO_6 (IO_6_out, I_Osel, ~I_Oadr[0], I_Oadr[1], I_Oadr[2], ~I_Oadr[3]);  // AND_Gate
  and IO_7 (IO_7_out, I_Osel, I_Oadr[0], I_Oadr[1], I_Oadr[2], ~I_Oadr[3]);  // AND_Gate
  Decoder #(.disabled(0)) decoder_7 (.out0(decoder_7_out0), .out1(decoder_7_out1), .sel(In_out_prime), .en(IO_7_out));
  Register #(.trigger("high")) register_3 (
    .D(I_Odat), .en(decoder_6_out0), .Q(register_3_q), .clk(decoder_6_out0));  // open: clr
  Register #(.trigger("high")) register_4 (
    .D(I_Odat), .en(decoder_7_out0), .Q(register_4_q), .clk(decoder_7_out0));  // open: clr
  assign I_Odat = decoder_6_out1 ? {{7{1'b0}}, or_2_out[0]} : 8'bz;  // Controlled_Buffer controlled_buffer_7
  assign I_Odat = decoder_7_out1 ? {{7{1'b0}}, X_O_X_out[0]} : 8'bz;  // Controlled_Buffer controlled_buffer_8
  and X_O_X (X_O_X_out[0], ~register_4_q[0], register_4_q[1], register_4_q[2], ~register_4_q[3], ~register_4_q[4], register_4_q[5]);  // AND_Gate
  and X_X_ (X_X__out, ~register_3_q[0], ~register_3_q[1], ~register_3_q[2], register_3_q[3], ~register_3_q[4], register_3_q[5]);  // AND_Gate
  and X___X (X___X_out, ~register_3_q[0], register_3_q[1], ~register_3_q[2], ~register_3_q[3], ~register_3_q[4], register_3_q[5]);  // AND_Gate
  and _X_X (_X_X_out, ~register_3_q[0], register_3_q[1], ~register_3_q[2], register_3_q[3], ~register_3_q[4], ~register_3_q[5]);  // AND_Gate
  or or_2 (or_2_out[0], _X_X_out, X___X_out, X_X__out);

  // Other names for the same wires on the sheet: rd_wr_prime = In_out_prime

  // Notes on the sheet:
  //   Tic-tac-toe
  //   contents of rom_1 (hex, n*v repeats v):
  //   cc f0 d2 2 d3 f3 bd 95 e3 6 99 b4 0 e1 6 d6 75 d2 f4 aa b9 99 e3 29 d0 8 d3 ce aa b9 74 ec 1c 1d f5
  //   b4 0 e1 1c ee 6c d2 f5 d6 a2 0 e1 5c 8e d6 a2 0 e1 5c 8e d1 3 d3 e0 d6 a6 0 e1 52 d1 5 b4 0 e0 6c d3
  //   cc d6 bd d6 bd 8f 8f d6 bd d6 bd d3 cd d6 bd d6 bd d6 bd d6 bd d1 4 89 e0 6c fc b0 0 e1 69 fd ee 6c
  //   8f ee 5e d2 1 d3 f3 d6 75 8e ee 6 a6 c1 c2 c3 d3 10 bd 8d ad 30 d3 4 77 ed 95 d2 f8 d6 a2 0 e1 95 d3
  //   10 bd d3 9 7d ec 95 d0 c0 c7 c6 c5 95 95 11 19 ad 0 e0 a1 d4 d7 d1 9 d3 ce 89 e0 bc c1 d6 c7 d6 c7
  //   d6 c7 a9 c5 b8 0 e0 ba 8b 8b 8b d7 ee a6 d7 8f 8f fd b4 0 c4 e0 6c c0 d7 fc b0 95 95 51 8f d7 0 1 2
  //   4 5 6 8 9 a 0 4 8 1 5 9 2 6 a 0 5 a 8 5 2
  //   RNG
  //   Attack logic
  //   Win|Lose
  //   Defend logic
  //   Bad strat fix
endmodule
